// Logisim project converter.circ as structural Verilog: 1 circuit, main circuit main
module main (
  input  [2:0] F1,
  input  [2:0] F2,
  input  [1:0] in_3,
  input  [2:0] F3,
  input  [1:0] CD,
  input  [1:0] BR,
  input  [7:0] AD
);

  wire clock_1_out;

  // Probe on {F1, F2, F3, CD, BR, AD}
  Clock clock_1 (.out(clock_1_out));
  RAM #(.addrWidth(2), .dataWidth(21), .bus("separate")) ram_1 (
    .addr(in_3), .din({F1, F2, F3, CD, BR, AD}), .str(1'b1), .clk(clock_1_out), .ld(1'b1));  // open: data, sel, clr
endmodule
